// Logisim project guia01_logisim.circ as structural Verilog: 1 circuit, main circuit main
module main (
  input  A,
  input  B,
  output out_3
);

  wire not_1_out, not_2_out;

  not not_1 (not_1_out, A);
  not not_2 (not_2_out, B);
  and and_1 (out_3, not_1_out, not_2_out);

  // Notes on the sheet:
  //   Pedro Henrique Cardoso Maia - 874398$
  //   Guia 0501 - (~a & ~b)
endmodule
