// Logisim project guia03_logisim.circ as structural Verilog: 1 circuit, main circuit main
module main (
  input  A,
  input  B,
  output S
);

  wire not_1_out, or_1_out;

  not not_1 (not_1_out, A);
  or or_1 (or_1_out, not_1_out, B);
  not not_2 (S, or_1_out);

  // Notes on the sheet:
  //   Pedro Henrique Cardoso Maia - 874398
  //   ~(~a | b)
endmodule
