// Logisim project guia04_logisim.circ as structural Verilog: 1 circuit, main circuit main
module main (
  input  A,
  input  B,
  output S
);

  wire and_1_out;

  and and_1 (and_1_out, A, B);
  not not_1 (S, and_1_out);

  // Notes on the sheet:
  //   Pedro Henrique Cardoso Maia - 874398
  //   ~(a & b)
endmodule
