// Logisim project guia05_logisim.circ as structural Verilog: 1 circuit, main circuit main
module main (
  input  A,
  input  B,
  output S
);

  wire xor_1_out;

  xor xor_1 (xor_1_out, A, B);
  not not_1 (S, xor_1_out);

  // Notes on the sheet:
  //   Pedro Henrique Cardoso Maia - 874398
  //   (~(a ^ b))
endmodule
