// Logisim project guia06_logisim.circ as structural Verilog: 1 circuit, main circuit main
module main (
  input  A,
  input  B,
  output S
);

  xor xor_1 (S, A, B);

  // Notes on the sheet:
  //   Pedro Henrique Cardoso Maia - 874398
  //   ((a ^ b))
endmodule
