// Logisim project guia07_logisim.circ as structural Verilog: 1 circuit, main circuit main
module main (
  input  A,
  input  B,
  output S
);

  wire nand_1_out, not_2_out;

  not not_1 (S, nand_1_out);
  nand nand_1 (nand_1_out, A, not_2_out);
  not not_2 (not_2_out, B);

  // Notes on the sheet:
  //   Pedro Henrique Cardoso Maia - 874398
  //   ((a ^ b))
endmodule
