// Logisim project guia08_logisim.circ as structural Verilog: 1 circuit, main circuit main
module main (
  input  A,
  input  B,
  output S
);

  wire not_1_out;

  not not_1 (not_1_out, A);
  or or_1 (S, not_1_out, B);

  // Notes on the sheet:
  //   Pedro Henrique Cardoso Maia - 874398
  //   ((a ^ b))
endmodule
