// Logisim project guia01ref.circ as structural Verilog: 1 circuit, main circuit main
module main (
  input  WE,
  input  D0,
  input  D1,
  input  D2,
  input  D3,
  input  OE,
  input  CLOCK,
  output Q0,
  output Q1,
  output Q2,
  output Q3
);

  wire and_1_out, and_2_out, and_3_out, and_4_out, and_5_out, and_6_out, and_7_out, and_8_out, F0_q, F1_q,
       F2_q, F3_q, not_1_out, not_2_out, not_3_out, undriven, undriven_2, undriven_3;

  not not_1 (not_1_out, D0);
  not not_2 (not_2_out, D1);
  not not_3 (not_3_out, D2);
  not not_4 (WE, D3);
  and and_1 (and_1_out, WE, D0);
  and and_2 (and_2_out, WE, not_1_out);
  and and_3 (and_3_out, WE, D1);
  and and_4 (and_4_out, WE, not_2_out);
  and and_5 (and_5_out, WE, D2);
  and and_6 (and_6_out, WE, not_3_out);
  and and_7 (and_7_out, WE, D3);
  and and_8 (and_8_out, WE, WE);
  J_K_Flip_Flop F0 (.J(and_1_out), .clk(CLOCK), .K(and_2_out), .Q(F0_q), .reset(undriven));  // open: Qn, preset
  J_K_Flip_Flop F1 (
    .J(and_3_out), .clk(CLOCK), .K(and_4_out), .Q(F1_q), .preset(undriven), .reset(undriven_2));  // open: Qn
  J_K_Flip_Flop F2 (
    .J(and_5_out), .clk(CLOCK), .K(and_6_out), .Q(F2_q), .preset(undriven_2), .reset(undriven_3));  // open: Qn
  J_K_Flip_Flop F3 (.clk(and_7_out), .K(and_8_out), .Q(F3_q), .preset(undriven_3));  // open: J, Qn, reset
  assign Q0 = OE ? F0_q : 1'bz;  // Controlled_Buffer controlled_buffer_1
  assign Q1 = OE ? F1_q : 1'bz;  // Controlled_Buffer controlled_buffer_2
  assign Q2 = OE ? F2_q : 1'bz;  // Controlled_Buffer controlled_buffer_3
  assign Q3 = OE ? F3_q : 1'bz;  // Controlled_Buffer controlled_buffer_4

  // Notes on the sheet:
  //   874398 - Pedro Henrique Cardoso Maia$
endmodule
