// Logisim project guia01.circ as structural Verilog: 1 circuit, main circuit main
module main (
  input  CLK,
  input  DATA,
  input  CLR,
  output out_4,
  output out_5,
  output out_6,
  output out_7,
  output out_8,
  output out_9
);

  D_Flip_Flop Q5 (.clk(CLK), .D(out_5), .Q(out_4), .reset(CLR));  // open: Qn, preset
  D_Flip_Flop Q4 (.clk(CLK), .D(out_6), .Q(out_5), .reset(CLR));  // open: Qn, preset
  D_Flip_Flop Q3 (.clk(CLK), .D(out_7), .Q(out_6), .reset(CLR));  // open: Qn, preset
  D_Flip_Flop Q2 (.clk(CLK), .D(out_8), .Q(out_7), .reset(CLR));  // open: Qn, preset
  D_Flip_Flop Q1 (.clk(CLK), .D(out_9), .Q(out_8), .reset(CLR));  // open: Qn, preset
  D_Flip_Flop Q0 (.clk(CLK), .D(DATA), .Q(out_9), .reset(CLR));  // open: Qn, preset

  // Notes on the sheet:
  //   Pedro Henrique Cardoso Maia - 874398
endmodule
