// Logisim project guia02.circ as structural Verilog: 1 circuit, main circuit main
module main (
  input  CLK,
  input  DATA,
  input  LOAD,
  input  CLR,
  output out_5,
  output out_6,
  output out_7,
  output out_8,
  output out_9,
  output out_10
);

  D_Flip_Flop d_ff_1 (.clk(CLK), .D(out_6), .Q(out_5), .preset(LOAD), .reset(CLR));  // open: Qn
  D_Flip_Flop d_ff_2 (.clk(CLK), .D(out_7), .Q(out_6), .preset(LOAD), .reset(CLR));  // open: Qn
  D_Flip_Flop d_ff_3 (.clk(CLK), .D(out_8), .Q(out_7), .preset(LOAD), .reset(CLR));  // open: Qn
  D_Flip_Flop d_ff_4 (.clk(CLK), .D(out_9), .Q(out_8), .preset(LOAD), .reset(CLR));  // open: Qn
  D_Flip_Flop d_ff_5 (.clk(CLK), .D(out_10), .Q(out_9), .preset(LOAD), .reset(CLR));  // open: Qn
  D_Flip_Flop d_ff_6 (.clk(CLK), .D(DATA), .Q(out_10), .preset(LOAD), .reset(CLR));  // open: Qn

  // Notes on the sheet:
  //   Pedro Henrique Cardoso Maia - 874398
endmodule
