// Logisim project guia03.circ as structural Verilog: 1 circuit, main circuit main
module main (
  input  INPUT,
  input  CLEAR,
  output out_3,
  output out_4,
  output out_5,
  output out_6,
  output out_7,
  output out_8
);

  wire CLK_out, multiplexer_1_out;

  Clock CLK (.out(CLK_out));
  Multiplexer #(.enable("false")) multiplexer_1 (.in0(out_4), .in1(1'b1), .out(multiplexer_1_out), .sel(INPUT));
  D_Flip_Flop Q0 (.clk(CLK_out), .D(out_4), .Q(out_3), .reset(CLEAR));  // open: Qn, preset
  D_Flip_Flop Q1 (.clk(CLK_out), .D(out_5), .Q(out_4), .reset(CLEAR));  // open: Qn, preset
  D_Flip_Flop Q2 (.clk(CLK_out), .D(out_6), .Q(out_5), .reset(CLEAR));  // open: Qn, preset
  D_Flip_Flop Q3 (.clk(CLK_out), .D(out_7), .Q(out_6), .reset(CLEAR));  // open: Qn, preset
  D_Flip_Flop Q4 (.clk(CLK_out), .D(out_8), .Q(out_7), .reset(CLEAR));  // open: Qn, preset
  D_Flip_Flop Q5 (.clk(CLK_out), .D(multiplexer_1_out), .Q(out_8), .reset(CLEAR));  // open: Qn, preset

  // Notes on the sheet:
  //   Pedro Henrique Cardoso Maia - 874398
endmodule
