// Logisim project guia04.circ as structural Verilog: 1 circuit, main circuit main
module main (
  input  INPUT,
  input  CLEAR,
  output out_3,
  output out_4,
  output out_5,
  output out_6,
  output out_7,
  output out_8
);

  wire clock_1_out, or_1_out;

  Clock clock_1 (.out(clock_1_out));
  or or_1 (or_1_out, INPUT, out_8);
  D_Flip_Flop d_ff_1 (.clk(clock_1_out), .D(or_1_out), .Q(out_3), .reset(CLEAR));  // open: Qn, preset
  D_Flip_Flop d_ff_2 (.clk(clock_1_out), .D(out_3), .Q(out_4), .reset(CLEAR));  // open: Qn, preset
  D_Flip_Flop d_ff_3 (.clk(clock_1_out), .D(out_4), .Q(out_5), .reset(CLEAR));  // open: Qn, preset
  D_Flip_Flop d_ff_4 (.clk(clock_1_out), .D(out_5), .Q(out_6), .reset(CLEAR));  // open: Qn, preset
  D_Flip_Flop d_ff_5 (.clk(clock_1_out), .D(out_6), .Q(out_7), .reset(CLEAR));  // open: Qn, preset
  D_Flip_Flop d_ff_6 (.clk(clock_1_out), .D(out_7), .Q(out_8), .reset(CLEAR));  // open: Qn, preset

  // Notes on the sheet:
  //   Pedro Henrique Cardoso Maia - 874398
endmodule
