// Logisim project guia05.circ as structural Verilog: 1 circuit, main circuit main
module main (
  input  CLR,
  input  CLEAR,
  input  LOAD,
  input  in_4,
  input  in_5,
  input  in_6,
  input  in_7,
  input  in_8,
  input  in_9,
  output out_10,
  output out_11,
  output out_12,
  output out_13,
  output out_14,
  output out_15,
  output out_16
);

  D_Flip_Flop d_ff_1 (.clk(CLR), .D(out_16), .Q(out_10), .reset(CLEAR));  // open: Qn, preset
  and and_1 (out_16, LOAD, in_4);
  and and_2 (out_10, LOAD, in_5);
  D_Flip_Flop d_ff_2 (.clk(CLR), .D(out_10), .Q(out_11), .reset(CLEAR));  // open: Qn, preset
  and and_3 (out_11, LOAD, in_6);
  D_Flip_Flop d_ff_3 (.clk(CLR), .D(out_11), .Q(out_12), .reset(CLEAR));  // open: Qn, preset
  D_Flip_Flop d_ff_4 (.clk(CLR), .D(out_12), .Q(out_13), .reset(CLEAR));  // open: Qn, preset
  and and_4 (out_12, LOAD, in_7);
  D_Flip_Flop d_ff_5 (.clk(CLR), .D(out_13), .Q(out_14), .reset(CLEAR));  // open: Qn, preset
  and and_5 (out_13, LOAD, in_8);
  and and_6 (out_14, LOAD, in_9);
  D_Flip_Flop d_ff_6 (.clk(CLR), .D(out_14), .Q(out_15), .reset(CLEAR));  // open: Qn, preset

  // Notes on the sheet:
  //   Pedro Henrique Cardoso Maia - 874398
endmodule
