// Logisim project guia06.circ as structural Verilog: 1 circuit, main circuit main
module main (
  input  INPUT,
  input  CLEAR,
  input  in_3,
  input  in_4,
  input  in_5,
  input  in_6,
  input  in_7,
  output out_8,
  output out_9,
  output out_10,
  output out_11,
  output out_12
);

  wire clock_1_out, or_2_out, or_3_out, or_4_out, or_5_out;

  Clock clock_1 (.out(clock_1_out));
  or or_1 (INPUT, or_2_out, in_3);
  D_Flip_Flop d_ff_1 (.clk(clock_1_out), .D(INPUT), .Q(out_8), .reset(CLEAR));  // open: Qn, preset
  D_Flip_Flop d_ff_2 (.clk(clock_1_out), .D(or_2_out), .Q(out_9), .reset(CLEAR));  // open: Qn, preset
  or or_2 (or_2_out, or_3_out, in_4);
  D_Flip_Flop d_ff_3 (.clk(clock_1_out), .D(or_3_out), .Q(out_10), .reset(CLEAR));  // open: Qn, preset
  or or_3 (or_3_out, or_4_out, in_5);
  or or_4 (or_4_out, CLEAR, in_6);
  D_Flip_Flop d_ff_4 (.clk(clock_1_out), .D(or_4_out), .Q(out_11), .reset(CLEAR));  // open: Qn, preset
  D_Flip_Flop d_ff_5 (.clk(clock_1_out), .D(or_5_out), .Q(out_12), .reset(CLEAR));  // open: Qn, preset
  or or_5 (or_5_out, out_8, in_7);

  // Notes on the sheet:
  //   Pedro Henrique Cardoso Maia -874398
endmodule
