// Logisim project pa02q04Da.circ as structural Verilog: 1 circuit, main circuit main
module main (
  input  a,
  input  b,
  input  c,
  output Da
);

  wire and_1_out, not_1_out, not_2_out;

  not not_1 (not_1_out, b);
  not not_2 (not_2_out, c);
  and and_1 (and_1_out, a, not_1_out, not_2_out);
  or or_1 (Da, and_1_out, not_1_out);

  // Notes on the sheet:
  //   Pedro Henrique Cardoso Maia - 874398
endmodule
