// Logisim project pa02q04SbRb.circ as structural Verilog: 1 circuit, main circuit main
module main (
  input  in_1,
  input  in_2,
  input  in_3,
  output Sb,
  output Rb
);

  wire not_1_out;

  not not_1 (not_1_out, in_2);
  and and_1 (Sb, not_1_out, in_3);

  assign Rb = in_1;

  // Notes on the sheet:
  //   Pedro Henrique Cardoso Maia - 874398
endmodule
