// Logisim project pa02q04Ta.circ as structural Verilog: 1 circuit, main circuit main
module main (
  input  a,
  input  b,
  input  c,
  output out_4
);

  wire and_1_out, and_2_out, not_1_out, not_2_out;

  not not_1 (not_1_out, a);
  not not_2 (not_2_out, b);
  and and_1 (and_1_out, not_1_out, not_2_out);
  and and_2 (and_2_out, a, not_2_out, c);
  or or_1 (out_4, and_1_out, and_2_out);

  // Notes on the sheet:
  //   Pedro Henrique Cardoso Maia - 874398
endmodule
