// Logisim project pa02q04Tb.circ as structural Verilog: 1 circuit, main circuit main
module main (
  input  in_1,
  input  in_2,
  input  in_3,
  output Tb
);

  wire xnor_1_out;

  xnor xnor_1 (xnor_1_out, in_1, in_2);
  and and_1 (Tb, xnor_1_out, in_3);

  // Notes on the sheet:
  //   Pedro Henrique Cardoso Maia - 874398
endmodule
