// Logisim project rec01q02.circ as structural Verilog: 1 circuit, main circuit main
module main (
  input  A,
  input  B,
  input  c,
  output S
);

  wire and_1_out, and_2_out, not_1_out, not_2_out;

  not not_1 (not_1_out, B);
  not not_2 (not_2_out, c);
  and and_1 (and_1_out, A, not_2_out);
  and and_2 (and_2_out, A, not_1_out, c);
  or or_1 (S, and_1_out, and_2_out);

  // Notes on the sheet:
  //   874398 - Pedro Henrique Cardoso Maia
endmodule
