// Logisim project rec01q03.circ as structural Verilog: 1 circuit, main circuit main
module main (
  input  A,
  input  B,
  input  C,
  output S
);

  wire not_1_out, or_1_out, or_2_out, or_3_out;

  not not_1 (not_1_out, A);
  or or_1 (or_1_out, not_1_out, C);
  or or_2 (or_2_out, A, B);
  or or_3 (or_3_out, B, C);
  and and_1 (S, or_1_out, or_2_out, or_3_out);

  // Notes on the sheet:
  //   874398 - Pedro Henrique Cardoso Maia
endmodule
