// Logisim project rec_0203.circ as structural Verilog: 1 circuit, main circuit main
module main (
  input  CLK,
  input  CLEAR,
  output out_3,
  output out_4,
  output out_5
);

  J_K_Flip_Flop j_k_ff_1 (.J(1'b1), .clk(CLK), .K(1'b1), .Q(out_5), .reset(CLEAR));  // open: Qn, preset
  J_K_Flip_Flop j_k_ff_2 (.J(1'b1), .clk(out_5), .K(1'b1), .Q(out_4), .reset(CLEAR));  // open: Qn, preset
  J_K_Flip_Flop j_k_ff_3 (.J(1'b1), .clk(out_4), .K(1'b1), .Q(out_3), .reset(CLEAR));  // open: Qn, preset

  // Notes on the sheet:
  //   874398 - Pedro Henrique Cardoso Maia
endmodule
