// Logisim project rec_0205.circ as structural Verilog: 1 circuit, main circuit main
module main (
  input  CLK1,
  input  CLEAR,
  output out_3,
  output out_4,
  output out_5
);

  wire not_1_out, not_2_out;

  J_K_Flip_Flop j_k_ff_1 (.J(1'b0), .clk(CLK1), .K(1'b1), .Q(out_5), .reset(CLEAR));  // open: Qn, preset
  not not_1 (not_1_out, out_5);
  J_K_Flip_Flop j_k_ff_2 (.J(out_5), .clk(CLK1), .K(not_1_out), .Q(out_4), .reset(CLEAR));  // open: Qn, preset
  not not_2 (not_2_out, out_4);
  J_K_Flip_Flop j_k_ff_3 (.J(out_4), .clk(CLK1), .K(not_2_out), .Q(out_3), .reset(CLEAR));  // open: Qn, preset

  // Notes on the sheet:
  //   874398 - Pedro Henrique Cardoso Maia
endmodule
