// Logisim project rec_0206.circ as structural Verilog: 1 circuit, main circuit main
module main (
  input  CLEAR,
  output out_2,
  output out_3,
  output out_4
);

  wire clock_1_out, not_1_out, not_2_out, not_3_out;

  Clock clock_1 (.out(clock_1_out));
  J_K_Flip_Flop j_k_ff_1 (.J(out_2), .clk(clock_1_out), .K(not_3_out), .Q(out_4), .reset(CLEAR));  // open: Qn, preset
  not not_1 (not_1_out, out_4);
  J_K_Flip_Flop j_k_ff_2 (.J(out_4), .clk(clock_1_out), .K(not_1_out), .Q(out_3), .reset(CLEAR));  // open: Qn, preset
  not not_2 (not_2_out, out_3);
  J_K_Flip_Flop j_k_ff_3 (.J(out_3), .clk(clock_1_out), .K(not_2_out), .Q(out_2), .reset(CLEAR));  // open: Qn, preset
  not not_3 (not_3_out, out_2);

  // Notes on the sheet:
  //   874398 - Pedro Henrique Cardoso Maia
endmodule
