// Logisim project 04.circ as structural Verilog: 1 circuit, main circuit main
module main (
  input  in_1,
  input  in_2,
  input  in_3,
  input  in_4,
  input  in_5,
  input  in_6,
  input  in_7,
  input  in_8,
  input  in_9,
  output out_10,
  output out_11,
  output out_12
);

  wire and_1_out, and_2_out, and_3_out, not_1_out, not_2_out, xor_1_out;

  not not_1 (not_1_out, in_3);
  not not_2 (not_2_out, in_5);
  and and_1 (and_1_out, in_1, not_1_out);
  and and_2 (and_2_out, in_2, in_3);
  and and_3 (and_3_out, in_1, in_2);
  and and_4 (out_11, not_2_out, in_7, in_9);
  or or_1 (out_10, and_1_out, and_2_out, and_3_out);
  xor xor_1 (xor_1_out, in_4, in_6);
  and and_5 (out_12, xor_1_out, in_8);

  // Notes on the sheet:
  //   Da
  //   Sa
  //   Ta
endmodule
